# Fritzing sketch hi5_detector (saved by Fritzing 0.9.0b)
breadboards: 1

parts:
  Part1 = Arduino Leonardo (Rev3b)
  R1 = Resistor [tolerance=±5% resistance=1M package="1206 [SMD]"]

nets:
  N1: Part1.5V, R1.Pin_0

notes:
  Person 1
  Person 2
