# Fritzing sketch physical_interface (saved by Fritzing 0.9.0b)
breadboards: 1

parts:
  Part1 = Arduino Leonardo (Rev3b)
  R1 = Resistor [tolerance=±5% resistance=1M package="1206 [SMD]"]
  R2 = Resistor [tolerance=±5% resistance=1M package="1206 [SMD]"]
  R3 = Resistor [tolerance=±5% resistance=1M package="1206 [SMD]"]
  R4 = Resistor [tolerance=±5% resistance=1M package="1206 [SMD]"]

nets:
  N1: Part1.5V, R1.Pin_0, R2.Pin_0, R3.Pin_0, R4.Pin_0
  N2: Part1.A1, R2.Pin_1
  N3: Part1.A2, R3.Pin_1
  N4: Part1.A3, R4.Pin_1

notes:
  Hand
  Button 1
  Button 2
  Button 3
  Button 4
