# Fritzing sketch servo_photoresistor (saved by Fritzing 0.9.0b)
breadboards: 1

parts:
  J1 = Basic Servo
  Part1 = Arduino Uno (Rev3) - ICSP
  R1 = Photocell (LDR) [package=THT]
  R2 = Resistor [tolerance=±5% resistance=220 package="0805 [SMD]"]

nets:
  GND: J1.gnd, Part1.GND, R2.Pin_1
  VCC: J1.vcc, Part1.5V
  N1: J1.pulse, Part1.D13/SCK
  N2: Part1.A1, R1.pin_0, R2.Pin_0
